# Fritzing sketch fritzing (saved by Fritzing 0.9.3b)
perfboards: 2

parts:
  U1 = ESP32S-HiLetgo [part_number=ESP32S-HiLetgo]
  IC1 = Voltage Regulator [package=to-220-alt]
  DHT1 = DHT11 Humitidy and Temperature Sensor
  LCD1 = AQM1602XA
  R1 = Resistor [tolerance=±5% resistance=75 package=THT]
  LED1 = RGB LED - (4 legs) [package="5 mm [THT]"]

nets:
  N1: U1.GPIO27, LED1.blue_cathode
  N2: U1.GPIO14, LED1.green_cathode
  N3: U1.GPIO12, R1.Pin_0
  GND: U1.GND, IC1.IN, DHT1.GND, LCD1.VSS, LED1.common_anode
  VDD: IC1.OUT, DHT1.VDD, LCD1.VDD
  N4: R1.Pin_1, LED1.red_cathode

custom parts:
  ESP32S-HiLetgo: HiLetgo ESP-WROOM-32 ESP32 ESP-32S Development Board 2.4GHz Dual-Mode WiFi + Bluetooth Dual Cores Microcontroller The ESP32 integrated with Antenna switches, RF Balun, power amplifiers, low-noise amplifiers, filters, and management modules, and the entire solution occupies the least area of PCB. 2.4 GHz Wi-Fi plus Bluetooth dual-mode chip, with TSMC Ultra-low power consumption 40nm technology,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
  DHT11 Humitidy and Temperature Sensor: DHT11 Humidity and Temperature Sensor
  AQM1602XA: A standard character display, usually with 2x16 characters. Comes in many colors.
