# Fritzing sketch trial_production (saved by Fritzing 0.9.3b)
breadboards: 1

parts:
  U1 = ESP32S-HiLetgo [part_number=ESP32S-HiLetgo]
  Part1 = Adafruit CCS811 [part_number="Adafruit #3566"]
  LCD1 = AQM1602XA
  Part2 = ws2812b [package=THT]

nets:
  VDD: U1.GPIO36, Part1.3.3V, LCD1.VDD, Part2.VDD
  GND: U1.GND, Part1.GND, LCD1.VSS, Part2.VSS
  N1: U1.GPIO16, Part2.DIN
  N2: U1.GPIO21, Part1.SDA, LCD1.SDA
  N3: U1.GPIO22, Part1.SCL, LCD1.SCL

custom parts:
  ESP32S-HiLetgo: HiLetgo ESP-WROOM-32 ESP32 ESP-32S Development Board 2.4GHz Dual-Mode WiFi + Bluetooth Dual Cores Microcontroller The ESP32 integrated with Antenna switches, RF Balun, power amplifiers, low-noise amplifiers, filters, and management modules, and the entire solution occupies the least area of PCB. 2.4 GHz Wi-Fi plus Bluetooth dual-mode chip, with TSMC Ultra-low power consumption 40nm technology,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
  Adafruit CCS811: Breathe easy - we finally have an I2C VOC/eCO2 sensor in the Adafruit shop! Add air quality monitoring to your project and with an Adafruit CCS811 Air Quality Sensor Breakout. This sensor from AMS is a gas sensor that can detect a wide range of Volatile Organic Compounds (VOCs) and is intended for indoor air quality monitoring. When connected to your microcontroller (running our library code)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
  AQM1602XA: A standard character display, usually with 2x16 characters. Comes in many colors.
